# Fritzing sketch Cool fan(can't change) (saved by Fritzing 0.9.3b)
breadboards: 1

parts:
  元件1 = Arduino Uno (Rev3)
  M1 = DC Motor
  Q1 = NPN-Transistor [package="TO92 [THT]"]
  R1 = Resistor [tolerance=±5% resistance=220 package=THT]
  D1 = Rectifier Diode [part_number=1N4001 package="300 mil [THT]"]

nets:
  N1: 元件1.D3_PWM, D1.cathode
  N2: 元件1.GND, M1.pin_2
  N3: 元件1.VIN, Q1.E
  N4: M1.pin_1, Q1.C
  N5: Q1.B, R1.Pin_1
  N6: R1.Pin_0, D1.anode
